# Fritzing sketch control de humedad en tierra final (saved by Fritzing 0.9.10b)

parts:
  부품1 = FC-28 Soil Hygrometer Module - Probe
  부품2 = FC-28 Soil Hygrometer Module
  부품3 = Arduino Uno (Rev3)
  WATER_PUMP1 = water pump/motor  # not connected
  KY-1 = Keyes Relay [package=THT]
  J1 = Screw terminal - 2 pins [package=THT]

nets:
  N1: 부품1.POS, 부품2.POS
  N2: 부품1.NEG, 부품2.NEG
  VCC: 부품2.VCC, 부품3.5V, KY-1.power
  GND: 부품2.GND, 부품3.GND, KY-1.ground
  N3: 부품2.AO, 부품3.A3
  N4: 부품3.D8, KY-1.signal
  N5: KY-1.C, J1.pin2

notes:
  220V C.A.
  BOMBA DE AGUAPARA RIEGO
  Higrómetro FC-28

custom parts:
  FC-28 Soil Hygrometer Module - Probe: The FC-28 is a soil hygrometer module that uses the Texas Instruments LM393 comparator chip to provide an analog measurement of soil humidity.
  FC-28 Soil Hygrometer Module: The FC-28 is a soil hygrometer module that uses the Texas Instruments LM393 comparator chip to provide an analog measurement of soil humidity. The digital output is high when soil moisture is over a certain threshold, as determined by adjusting the potentiometer.
  water pump/motor: WATER PUMP BY ARDUBLOCKTR
  Keyes Relay: The Keyes 5V relay module is suitable for SCM development, home appliance control. It uses a 5V~12V TIL control signal which can control DC / AC signal.
