# Fritzing sketch control de intensidad de luces - invernadero (saved by Fritzing 0.9.10b)
breadboards: 1

parts:
  U1 = WS2812 RGB LED strip
  Componente2 = Arduino Uno (Rev3)
  R2 = Resistor [tolerance=±5% power=0.25 resistance=330 package=THT]
  Q2 = TIP120 Hi-Current Darlington Transistor
  Mod2 = KY-018 Photoresistor Module [package="Breakout board"]
  J2 = Screw terminal - 2 pins [package=THT]

nets:
  N1: U1.GND, Q2.COLLECTOR
  N2: U1.DIN, J2.pin1
  N3: Componente2.A2, Mod2.S
  N4: Componente2.D11_PWM/MOSI, R2.Pin_0
  GND: Componente2.GND, Q2.EMITTER, Mod2.Vin, Mod2.-, J2.pin2
  N5: R2.Pin_1, Q2.BASE

notes:
  12V C.C.

custom parts:
  WS2812 RGB LED strip: WS2812 strip
  KY-018 Photoresistor Module: KY-018 Photoresistor module, used to measure light intensity. It can determine the presence or absence of light.
