# Fritzing sketch control de temperatura del invernadero DHT22 (saved by Fritzing 0.9.10b)
breadboards: 2

parts:
  J1 = DHT22 temperature-humidity sensor [form="♂ (male)" package=THT]
  J2 = Peltier Element
  KY-1 = Keyes Relay [package=THT]
  F1 = Fan - Ventilador [package=THT]
  F2 = Fan - Ventilador [package=THT]
  Componente1 = Arduino Uno (Rev3)
  J3 = Screw terminal - 2 pins [package=THT]
  Q2 = TIP120 Hi-Current Darlington Transistor
  R1 = Resistor [tolerance=±5% power=0.25 resistance=330 package=THT]
  D1 = Diode [package=diode-hv]  # not connected
  J4 = Screw terminal - 2 pins [package=THT]  # not connected
  Componente2 = LCD1602-I2C
  R2 = Resistor [tolerance=±5% power=0.25 resistance=220 package=THT]
  R3 = Resistor [tolerance=±5% power=0.25 resistance=220 package=THT]
  R4 = Resistor [tolerance=±5% power=0.25 resistance=220 package=THT]
  LED1 = LED - 5mm [color="Red (633nm)" current=0.030 package="5 mm [THT]"]
  LED2 = LED - 5mm [color="Yellow (595nm)" current=0.030 package="5 mm [THT]"]
  LED3 = LED - 5mm [color="Green (570nm)" current=0.030 package="5 mm [THT]"]

nets:
  VCC: J1.VCC, KY-1.power, Componente1.5V, Componente2.VCC
  N1: J1.OUT, Componente1.D7
  GND: J1.GND, KY-1.ground, Componente1.GND, Q2.EMITTER, Componente2.GND, LED1.cathode, LED2.cathode, LED3.cathode
  N2: J2.pin1, KY-1.NC
  N3: J2.pin2, J3.pin1
  N4: KY-1.signal, Componente1.D13/SCK
  5V: F1.5V, F2.5V
  GND_2: F1.GND, F2.GND
  N5: Componente1.A4/SDA, Componente2.SDA
  N6: Componente1.A5/SCL, Componente2.SCL
  N7: Componente1.D12/MISO, R1.Pin_0
  N8: Componente1.D2, R4.Pin_0
  N9: Componente1.D3_PWM, R3.Pin_0
  N10: Componente1.D4, R2.Pin_0
  N11: Q2.BASE, R1.Pin_1
  N12: R2.Pin_1, LED2.anode
  N13: R3.Pin_1, LED3.anode
  N14: R4.Pin_1, LED1.anode

notes:
  12V C.C.
  CELDA DE PELTIER
  DHT 22
  Módulo de Relé
  LCD - 16 x 2  - Bus I2C

custom parts:
  DHT22 temperature-humidity sensor: The DHT22 is a basic, low-cost digital temperature and humidity sensor. It uses a capacitive humidity sensor and a thermistor to measure the surrounding air, and spits out a digital signal on the data pin (no analog input pins needed). It's fairly simple to use, but requires careful timing to grab data. The only real downside of this sensor is you can only get new data from it once every 2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
  Keyes Relay: The Keyes 5V relay module is suitable for SCM development, home appliance control. It uses a 5V~12V TIL control signal which can control DC / AC signal.
  Fan - Ventilador: Ventilador de 2 pines, se encuentra comunmente en computadoras de escritorio
  LCD1602-I2C: A standard character display, usually with 2x16 characters. Comes in many colors with LCM1602 IIC attached.
